// Logisim project bonkpu.circ as structural Verilog: 4 circuits, main circuit main
module main (
);

  wire AI, and_1_out, AO, BI, BO, button_1_out, CE, CI, CLK, clock_1_out, CO, dipswitch_1_p2, EO, FI, HLT,
       IE, II, MI, MS0, MU, nor_2_out, not_1_out, OC, OI, RI, RO, SO, SU, XI, XM, XO, xor_2_out;
  wire [1:0] STACK_MODE;
  wire [2:0] FLAGS, nor_1_out;
  wire [3:0] MICROSTEP_q;
  wire [7:0] A_REG_q, adder_1_out, B_REG_q, dipswitch_1_p1, mar_1_addr, MEM_dout, microcode_b_data,
       multiplexer_1_out, OP_REG_q, stack_pointer_1_out_bus, X_REG_q, xor_1_out;

  Counter #(.max('hf), .width(4)) MICROSTEP (
    .load(IE), .clk(not_1_out), .D(4'b0000), .Q(MICROSTEP_q));  // open: clr, up, count, carry
  not not_1 (not_1_out, CLK);
  Register OP_REG (.D(stack_pointer_1_out_bus), .en(II), .clk(CLK), .Q(OP_REG_q));  // open: clr
  RAM #(.enables("line")) MEM (.addr(mar_1_addr), .we(RI), .clk(CLK), .din(stack_pointer_1_out_bus), .dout(MEM_dout));
  Comparator #(.mode("unsigned"), .width(4)) comparator_1 (.a(MICROSTEP_q), .b(4'b0000), .eq(MS0));  // open: gt, lt
  ROM #(.addrWidth(15)) microcode_a (
    .addr({FLAGS, OP_REG_q, MICROSTEP_q}), .data({IE, CE, MU, XM, SU, FI, STACK_MODE}));
  stack_pointer stack_pointer_1 (.LO(SO), .CLK(CLK), .MODE(STACK_MODE), .out_bus(stack_pointer_1_out_bus));
  program_counter program_counter_1 (
    .CE(CE), .CLK(CLK), .I(CI), .O(CO), .bus_in(stack_pointer_1_out_bus), .bus_out(stack_pointer_1_out_bus));
  mar mar_1 (.CLK(CLK), .I(MI), .OI(OI), .OC(OC), .bus_in(stack_pointer_1_out_bus), .U(MU), .addr(mar_1_addr));
  LedBar ledbar_1 (
    .led0(stack_pointer_1_out_bus[7]), .led1(stack_pointer_1_out_bus[6]), .led2(stack_pointer_1_out_bus[5]),
    .led3(stack_pointer_1_out_bus[4]), .led4(stack_pointer_1_out_bus[3]), .led5(stack_pointer_1_out_bus[2]),
    .led6(stack_pointer_1_out_bus[1]), .led7(stack_pointer_1_out_bus[0]));
  Register X_REG (.D(stack_pointer_1_out_bus), .en(XI), .clk(CLK), .Q(X_REG_q));  // open: clr
  Pull_Resistor pull_resistor_1 (.node(stack_pointer_1_out_bus));
  Register A_REG (.D(stack_pointer_1_out_bus), .en(AI), .clk(CLK), .Q(A_REG_q));  // open: clr
  assign stack_pointer_1_out_bus = AO ? A_REG_q : 8'bz;  // Controlled_Buffer controlled_buffer_1
  assign stack_pointer_1_out_bus = EO ? adder_1_out : 8'bz;  // Controlled_Buffer EO_GATE
  assign stack_pointer_1_out_bus = RO ? MEM_dout : 8'bz;  // Controlled_Buffer controlled_buffer_2
  Register B_REG (.D(stack_pointer_1_out_bus), .en(BI), .clk(CLK), .Q(B_REG_q));  // open: clr
  LedBar #(.matrixcols(16)) ledbar_2 (
    .led0(IE), .led1(CE), .led2(MU), .led3(XM), .led4(SU), .led5(FI), .led6(STACK_MODE[1]),
    .led7(STACK_MODE[0]), .led8(microcode_b_data[7]), .led9(microcode_b_data[6]),
    .led10(microcode_b_data[5]), .led11(microcode_b_data[4]), .led12(microcode_b_data[3]),
    .led13(microcode_b_data[2]), .led14(microcode_b_data[1]), .led15(microcode_b_data[0]));
  ROM #(.addrWidth(15)) microcode_b (.addr({FLAGS, OP_REG_q, MICROSTEP_q}), .data(microcode_b_data));
  assign stack_pointer_1_out_bus = XO ? X_REG_q : 8'bz;  // Controlled_Buffer controlled_buffer_3
  assign stack_pointer_1_out_bus = BO ? B_REG_q : 8'bz;  // Controlled_Buffer B_GATE
  // Probe on X_REG_q
  // Probe on X_REG_q
  // Probe on A_REG_q
  // Probe on A_REG_q
  Multiplexer #(.width(8)) multiplexer_1 (.in0({8{1'b0}}), .in1({8{1'b1}}), .out(multiplexer_1_out), .sel(SU));
  // Probe on B_REG_q
  // Probe on B_REG_q
  Button button_1 (.out(button_1_out));
  // DipSwitch #(.number(2)) dipswitch_1: pin names not known; wires that end beside it: dipswitch_1_p1, dipswitch_1_p2
  Multiplexer #(.width(8)) multiplexer_2 (.in0(A_REG_q), .in1(X_REG_q), .out(dipswitch_1_p1), .sel(XM));
  assign xor_1_out = multiplexer_1_out ^ B_REG_q;  // XOR_Gate xor_1, 8 bits wide
  xor xor_2 (xor_2_out, button_1_out, dipswitch_1_p2);
  Adder adder_1 (.a(dipswitch_1_p1), .b(xor_1_out), .out(adder_1_out), .cin(SU), .cout(nor_1_out[2]));
  and and_1 (and_1_out, MS0, xor_2_out);
  nor nor_1 (nor_1_out[0], adder_1_out[0], adder_1_out[1], adder_1_out[2], adder_1_out[3], adder_1_out[4], adder_1_out[5], adder_1_out[6], adder_1_out[7]);
  // Probe on adder_1_out
  // Probe on adder_1_out
  Decoder #(.enable("false"), .select(4)) decoder_1 (
    .out1(RO), .out2(AO), .out3(BO), .out4(EO), .out5(CO), .out6(SO), .out7(XO), .out15(HLT),
    .sel(microcode_b_data[3:0]));  // open: out0, out8, out9, out10, out11, out12, out13, out14
  Decoder #(.enable("false"), .select(4)) decoder_2 (
    .out1(RI), .out2(AI), .out3(BI), .out4(II), .out5(CI), .out6(MI), .out7(OI), .out8(OC), .out9(XI),
    .sel(microcode_b_data[7:4]));  // open: out0, out10, out11, out12, out13, out14, out15
  Clock clock_1 (.out(clock_1_out));
  nor nor_2 (nor_2_out, HLT, and_1_out);
  Register #(.width(3)) FLAG_REG (
    .D({nor_1_out[2], adder_1_out[7], nor_1_out[0]}), .en(FI), .clk(CLK), .Q(FLAGS));  // open: clr
  // Probe on microcode_b_data[3:0]
  // Probe on microcode_b_data[7:4]
  and and_2 (CLK, clock_1_out, nor_2_out);
  LedBar #(.matrixcols(3)) ledbar_3 (.led0(FLAGS[2]), .led1(FLAGS[1]), .led2(FLAGS[0]));

  // Notes on the sheet:
  //   contents of microcode_a (hex, n*v repeats v):
  //   20 c0 14*0 20 40 20 c0 12*0 20 40 20 60 80 11*0 20 40 20 60 20 80 10*0 20 40 20 40 20 0 80 9*0 20 40
  //   20 40 20 40 20 0 80 7*0 20 40 20 40 20 40 20 30 80 7*0 20 40 20 60 80 11*0 20 40 20 60 20 80 10*0 20
  //   40 20 40 20 0 80 9*0 20 40 20 40 84 11*0 20 40 20 60 0 84 10*0 20 40 20 40 20 0 4 80 8*0 20 40 20 40
  //   8c 11*0 20 40 20 60 0 8c 10*0 20 40 20 40 20 0 c 80 8*0 20 40 20 40 8c 11*0 20 40 20 60 0 8c 10*0 20
  //   40 20 40 20 0 8c 9*0 20 40 20 c0 12*0 20 40 c0 13*0 20 40 20 c0 12*0 20 40 c0 13*0 20 40 20 c0 12*0
  //   20 40 c0 13*0 20 40 20 c0 12*0 20 40 81 13*0 20 40 83 13*0 20 40 82 13*0 20 40 20 83 12*0 20 40 20
  //   40 20 83 10*0 20 40 2 20 80 11*0 20 40 20 3 20 c0 10*0 20 40 2 20 0 c0 10*0 20 40 80 13*0 20 c0 14*0
  //   20 c0 14*0 20 c0 14*0 20 c0 14*0 20 c0 14*0 20 c0 14*0 20 c0 14*0 20 c0 14*0 20 c0 14*0 20 c0 14*0
  //   20 c0 14*0 20 c0 14*0 20 c0 14*0 20 c0 14*0 20 c0 14*0 20 c0 14*0 20 c0 14*0 20 c0 14*0 20 c0 14*0
  //   20 c0 14*0 20 c0 14*0 20 c0 14*0 20 c0 14*0 20 c0 14*0 20 c0 14*0 20 c0 14*0 20 c0 14*0 20 c0 14*0
  //   20 c0 14*0 20 c0 14*0 20 c0 14*0 20 c0 14*0 20 c0 14*0 20 c0 14*0 20 c0 14*0 20 c0 14*0 20 c0 14*0
  //   20 c0 14*0 20 c0 14*0 20 c0 14*0 20 c0 14*0 20 c0 14*0 20 c0 14*0 20 c0 14*0 20 c0 14*0 20 c0 14*0
  //   20 c0 14*0 20 c0 14*0 20 c0 14*0 20 c0 14*0 20 c0 14*0 20 c0 14*0 20 c0 14*0 20 c0 14*0 20 c0 14*0
  //   20 c0 14*0 20 c0 14*0 20 c0 14*0 20 c0 14*0 20 c0 14*0 20 c0 14*0 20 c0 14*0 20 c0 14*0 20 c0 14*0
  //   20 c0 14*0 20 c0 14*0 20 c0 14*0 20 c0 14*0 20 c0 14*0 20 c0 14*0 20 c0 14*0 20 c0 14*0 20 c0 14*0
  //   20 c0 14*0 20 c0 14*0 20 c0 14*0 20 c0 14*0 20 c0 14*0 20 c0 14*0 20 c0 14*0 20 c0 14*0 20 c0 14*0
  //   20 c0 14*0 20 c0 14*0 20 c0 14*0 20 c0 14*0 20 c0 14*0 20 c0 14*0 20 c0 14*0 20 c0 14*0 20 c0 14*0
  //   20 c0 14*0 20 c0 14*0 20 c0 14*0 20 c0 14*0 20 c0 14*0 20 c0 14*0 20 c0 14*0 20 c0 14*0 20 c0 14*0
  //   20 c0 14*0 20 c0 14*0 20 c0 14*0 20 c0 14*0 20 c0 14*0 20 c0 14*0 20 c0 14*0 20 c0 14*0 20 c0 14*0
  //   20 c0 14*0 20 c0 14*0 20 c0 14*0 20 c0 14*0 20 c0 14*0 20 c0 14*0 20 c0 14*0 20 c0 14*0 20 c0 14*0
  //   20 c0 14*0 20 c0 14*0 20 c0 14*0 20 c0 14*0 20 c0 14*0 20 c0 14*0 20 c0 14*0 20 c0 14*0 20 c0 14*0
  //   20 c0 14*0 20 c0 14*0 20 c0 14*0 20 c0 14*0 20 c0 14*0 20 c0 14*0 20 c0 14*0 20 c0 14*0 20 c0 14*0
  //   20 c0 14*0 20 c0 14*0 20 c0 14*0 20 c0 14*0 20 c0 14*0 20 c0 14*0 20 c0 14*0 20 c0 14*0 20 c0 14*0
  //   20 c0 14*0 20 c0 14*0 20 c0 14*0 20 c0 14*0 20 c0 14*0 20 c0 14*0 20 c0 14*0 20 c0 14*0 20 c0 14*0
  //   20 c0 14*0 20 c0 14*0 20 c0 14*0 20 c0 14*0 20 c0 14*0 20 c0 14*0 20 c0 14*0 20 c0 14*0 20 c0 14*0
  //   20 c0 14*0 20 c0 14*0 20 c0 14*0 20 c0 14*0 20 c0 14*0 20 c0 14*0 20 c0 14*0 20 c0 14*0 20 c0 14*0
  //   20 c0 14*0 20 c0 14*0 20 c0 14*0 20 c0 14*0 20 c0 14*0 20 c0 14*0 20 c0 14*0 20 c0 14*0 20 c0 14*0
  //   20 c0 14*0 20 c0 14*0 20 c0 14*0 20 c0 14*0 20 c0 14*0 20 c0 14*0 20 c0 14*0 20 c0 14*0 20 c0 14*0
  //   20 c0 14*0 20 c0 14*0 20 c0 14*0 20 c0 14*0 20 c0 14*0 20 c0 14*0 20 c0 14*0 20 c0 14*0 20 c0 14*0
  //   20 c0 14*0 20 c0 14*0 20 c0 14*0 20 c0 14*0 20 c0 14*0 20 c0 14*0 20 c0 14*0 20 c0 14*0 20 c0 14*0
  //   20 c0 14*0 20 c0 14*0 20 c0 14*0 20 c0 14*0 20 c0 14*0 20 c0 14*0 20 c0 14*0 20 c0 14*0 20 c0 14*0
  //   20 c0 14*0 20 c0 14*0 20 c0 14*0 20 c0 14*0 20 c0 14*0 20 40 20 c0 12*0 20 40 20 60 80 11*0 20 40 20
  //   60 20 80 10*0 20 40 20 40 20 0 80 9*0 20 40 20 40 20 40 20 0 80 7*0 20 40 20 40 20 40 20 30 80 7*0
  //   20 40 20 60 80 11*0 20 40 20 60 20 80 10*0 20 40 20 40 20 0 80 9*0 20 40 20 40 84 11*0 20 40 20 60 0
  //   84 10*0 20 40 20 40 20 0 4 80 8*0 20 40 20 40 8c 11*0 20 40 20 60 0 8c 10*0 20 40 20 40 20 0 c 80
  //   8*0 20 40 20 40 8c 11*0 20 40 20 60 0 8c 10*0 20 40 20 40 20 0 8c 9*0 20 40 20 c0 12*0 20 40 20 c0
  //   12*0 20 40 c0 13*0 20 40 c0 13*0 20 40 20 c0 12*0 20 40 c0 13*0 20 40 20 c0 12*0 20 40 81 13*0 20 40
  //   83 13*0 20 40 82 13*0 20 40 20 83 12*0 20 40 20 40 20 83 10*0 20 40 2 20 80 11*0 20 40 20 3 20 c0
  //   10*0 20 40 2 20 0 c0 10*0 20 40 80 13*0 20 c0 14*0 20 c0 14*0 20 c0 14*0 20 c0 14*0 20 c0 14*0 20 c0
  //   14*0 20 c0 14*0 20 c0 14*0 20 c0 14*0 20 c0 14*0 20 c0 14*0 20 c0 14*0 20 c0 14*0 20 c0 14*0 20 c0
  //   14*0 20 c0 14*0 20 c0 1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
  //   contents of microcode_b (hex, n*v repeats v):
  //   65 41 14*0 65 41 65 21 12*0 65 41 65 61 21 11*0 65 41 65 61 61 21 10*0 65 41 65 71 66 21 80 9*0 65
  //   41 65 31 65 63 71 21 80 7*0 65 41 65 91 65 71 66 64 21 7*0 65 41 65 61 12 11*0 65 41 65 61 61 12
  //   10*0 65 41 65 71 66 12 80 9*0 65 41 65 31 24 11*0 65 41 65 61 31 24 10*0 65 41 65 71 66 31 24 80 8*0
  //   65 41 65 31 24 11*0 65 41 65 61 31 24 10*0 65 41 65 71 66 31 24 80 8*0 65 41 65 31 12*0 65 41 65 61
  //   31 11*0 65 41 65 71 66 31 80 9*0 65 41 65 51 12*0 65 41 14*0 65 41 65 51 12*0 65 41 14*0 65 41 65 51
  //   12*0 65 41 14*0 65 41 65 51 12*0 65 41 14*0 65 41 14*0 65 41 14*0 65 41 66 12 12*0 65 41 65 31 66 13
  //   10*0 65 41 0 66 21 11*0 65 41 66 15 65 51 10*0 65 41 0 66 51 11*0 65 41 f 13*0 65 41 14*0 65 41 14*0
  //   65 41 14*0 65 41 14*0 65 41 14*0 65 41 14*0 65 41 14*0 65 41 14*0 65 41 14*0 65 41 14*0 65 41 14*0
  //   65 41 14*0 65 41 14*0 65 41 14*0 65 41 14*0 65 41 14*0 65 41 14*0 65 41 14*0 65 41 14*0 65 41 14*0
  //   65 41 14*0 65 41 14*0 65 41 14*0 65 41 14*0 65 41 14*0 65 41 14*0 65 41 14*0 65 41 14*0 65 41 14*0
  //   65 41 14*0 65 41 14*0 65 41 14*0 65 41 14*0 65 41 14*0 65 41 14*0 65 41 14*0 65 41 14*0 65 41 14*0
  //   65 41 14*0 65 41 14*0 65 41 14*0 65 41 14*0 65 41 14*0 65 41 14*0 65 41 14*0 65 41 14*0 65 41 14*0
  //   65 41 14*0 65 41 14*0 65 41 14*0 65 41 14*0 65 41 14*0 65 41 14*0 65 41 14*0 65 41 14*0 65 41 14*0
  //   65 41 14*0 65 41 14*0 65 41 14*0 65 41 14*0 65 41 14*0 65 41 14*0 65 41 14*0 65 41 14*0 65 41 14*0
  //   65 41 14*0 65 41 14*0 65 41 14*0 65 41 14*0 65 41 14*0 65 41 14*0 65 41 14*0 65 41 14*0 65 41 14*0
  //   65 41 14*0 65 41 14*0 65 41 14*0 65 41 14*0 65 41 14*0 65 41 14*0 65 41 14*0 65 41 14*0 65 41 14*0
  //   65 41 14*0 65 41 14*0 65 41 14*0 65 41 14*0 65 41 14*0 65 41 14*0 65 41 14*0 65 41 14*0 65 41 14*0
  //   65 41 14*0 65 41 14*0 65 41 14*0 65 41 14*0 65 41 14*0 65 41 14*0 65 41 14*0 65 41 14*0 65 41 14*0
  //   65 41 14*0 65 41 14*0 65 41 14*0 65 41 14*0 65 41 14*0 65 41 14*0 65 41 14*0 65 41 14*0 65 41 14*0
  //   65 41 14*0 65 41 14*0 65 41 14*0 65 41 14*0 65 41 14*0 65 41 14*0 65 41 14*0 65 41 14*0 65 41 14*0
  //   65 41 14*0 65 41 14*0 65 41 14*0 65 41 14*0 65 41 14*0 65 41 14*0 65 41 14*0 65 41 14*0 65 41 14*0
  //   65 41 14*0 65 41 14*0 65 41 14*0 65 41 14*0 65 41 14*0 65 41 14*0 65 41 14*0 65 41 14*0 65 41 14*0
  //   65 41 14*0 65 41 14*0 65 41 14*0 65 41 14*0 65 41 14*0 65 41 14*0 65 41 14*0 65 41 14*0 65 41 14*0
  //   65 41 14*0 65 41 14*0 65 41 14*0 65 41 14*0 65 41 14*0 65 41 14*0 65 41 14*0 65 41 14*0 65 41 14*0
  //   65 41 14*0 65 41 14*0 65 41 14*0 65 41 14*0 65 41 14*0 65 41 14*0 65 41 14*0 65 41 14*0 65 41 14*0
  //   65 41 14*0 65 41 14*0 65 41 14*0 65 41 14*0 65 41 14*0 65 41 14*0 65 41 14*0 65 41 14*0 65 41 14*0
  //   65 41 14*0 65 41 14*0 65 41 14*0 65 41 14*0 65 41 14*0 65 41 14*0 65 41 14*0 65 41 14*0 65 41 14*0
  //   65 41 14*0 65 41 14*0 65 41 14*0 65 41 14*0 65 41 14*0 65 41 14*0 65 41 14*0 65 41 14*0 65 41 14*0
  //   65 41 14*0 65 41 14*0 65 41 14*0 65 41 14*0 65 41 14*0 65 41 14*0 65 41 14*0 65 41 14*0 65 41 14*0
  //   65 41 14*0 65 41 14*0 65 41 14*0 65 41 14*0 65 41 14*0 65 41 14*0 65 41 14*0 65 41 14*0 65 41 14*0
  //   65 41 14*0 65 41 14*0 65 41 14*0 65 41 14*0 65 41 14*0 65 41 14*0 65 41 14*0 65 41 14*0 65 41 14*0
  //   65 41 14*0 65 41 14*0 65 41 14*0 65 41 14*0 65 41 65 21 12*0 65 41 65 61 21 11*0 65 41 65 61 61 21
  //   10*0 65 41 65 71 66 21 80 9*0 65 41 65 31 65 63 71 21 80 7*0 65 41 65 91 65 71 66 64 21 7*0 65 41 65
  //   61 12 11*0 65 41 65 61 61 12 10*0 65 41 65 71 66 12 80 9*0 65 41 65 31 24 11*0 65 41 65 61 31 24
  //   10*0 65 41 65 71 66 31 24 80 8*0 65 41 65 31 24 11*0 65 41 65 61 31 24 10*0 65 41 65 71 66 31 24 80
  //   8*0 65 41 65 31 12*0 65 41 65 61 31 11*0 65 41 65 71 66 31 80 9*0 65 41 65 51 12*0 65 41 65 51 12*0
  //   65 41 14*0 65 41 14*0 65 41 65 51 12*0 65 41 14*0 65 41 65 51 12*0 65 41 14*0 65 41 14*0 65 41 14*0
  //   65 41 66 12 12*0 65 41 65 31 66 13 10*0 65 41 0 66 21 11*0 65 41 66 15 65 51 10*0 65 41 0 66 51 11*0
  //   65 41 f 13*0 65 41 14*0 65 41 14*0 65 41 14*0 65 41 14*0 65 41 14*0 65 41 14*0 65 41 14*0 65 41 14*0
  //   65 41 14*0 65 41 14*0 65 41 14*0 65 41 14*0 65 41 14*0 65 41 14*0 65 41 14*0 65 41 14*0 65 41 14*0
  //   65 41 14*0 65 41 14*0 65 4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
endmodule

module stack_pointer (
  input  CLK,
  input  [1:0] MODE,
  input  LO,
  output [7:0] out_bus
);

  wire decoder_1_out0, decoder_1_out1, decoder_1_out2, decoder_1_out3, or_1_out;
  wire [7:0] counter_1_q;

  Decoder #(.enable("false"), .select(2)) decoder_1 (
    .out0(decoder_1_out0), .out1(decoder_1_out1), .out2(decoder_1_out2), .out3(decoder_1_out3), .sel(MODE));
  // NoConnect on decoder_1_out0
  LED INC (.in(decoder_1_out2));
  LED DEC (.in(decoder_1_out3));
  LED LOAD (.in(decoder_1_out1));
  or or_1 (or_1_out, decoder_1_out1, decoder_1_out2, decoder_1_out3);
  Counter counter_1 (
    .load(decoder_1_out1), .up(decoder_1_out2), .count(or_1_out), .clk(CLK), .D({8{1'b1}}), .Q(counter_1_q));  // open: clr, carry
  assign out_bus = LO ? counter_1_q : 8'bz;  // Controlled_Buffer controlled_buffer_1
endmodule

module program_counter (
  input  I,
  input  CE,
  input  CLK,
  input  O,
  input  [7:0] bus_in,
  output [7:0] bus_out
);

  wire or_1_out;
  wire [7:0] C_q;

  or or_1 (or_1_out, I, CE);
  Counter C (.load(I), .count(or_1_out), .clk(CLK), .D(bus_in), .Q(C_q));  // open: clr, up, carry
  assign bus_out = O ? C_q : 8'bz;  // Controlled_Buffer controlled_buffer_1
endmodule

module mar (
  input  [7:0] bus_in,
  input  CLK,
  input  I,
  input  U,
  input  OI,
  input  OC,
  output [7:0] addr
);

  wire [7:0] A_q, adder_1_out, O_q;

  Register A (.D(bus_in), .en(I), .clk(CLK), .Q(A_q));  // open: clr
  Register O (.D(bus_in), .en(OI), .clk(CLK), .Q(O_q), .clr(OC));
  Adder adder_1 (.a(A_q), .b(O_q), .out(adder_1_out));  // open: cin, cout
  Register #(.trigger("high")) MARV (.D(adder_1_out), .en(U), .clk(CLK), .Q(addr));  // open: clr
endmodule
